# Fritzing sketch esp8266_garage_door (saved by Fritzing 0.9.4)

parts:
  U1 = NodeMCU V3.0
  Mod1 = KY-019 5V Relay Module [package="Breakout board"]
  S1 = Reed switch [package=THT]

nets:
  N1: U1.D2, S1.pin_2
  N2: U1.GND#6, U1.GND#13, Mod1.-
  N3: U1.D7, Mod1.S
  N4: U1.Vin, Mod1.+
  N5: U1.GND#41, S1.pin_1

notes:
  to garage door

custom parts:
  NodeMCU V3.0: ESP8266 based NodeMCU
  KY-019 5V Relay Module: KY-019 5V Relay module, used to control AC circuits. (Special thanks to vanepp for fixing the PCB holes and other errors)
