# Fritzing sketch garage_doors (saved by Fritzing 0.9.4)

parts:
  Raspberry_Pi_1 = Raspberry Pi 3 [part_number=RPI-3-V1.2]
  Right_door_sensor = Reed switch [package=THT]
  Left_door_sensor = Reed switch [package=THT]
  SI7021_temperature_sensor = Humidity Temperature Sensor SI7021
  2-Channel_Relay = 2-Channel 5v Relay Shield [package=relay-2ch5v10a]

nets:
  N1: Raspberry_Pi_1.GPIO2, SI7021_temperature_sensor.SDA
  N2: Raspberry_Pi_1.GPIO3, SI7021_temperature_sensor.SCL
  N3: Raspberry_Pi_1.GPIO17, 2-Channel_Relay.IN1
  N4: Raspberry_Pi_1.GPIO27, 2-Channel_Relay.IN2
  3V3: Raspberry_Pi_1.3V3, SI7021_temperature_sensor.VCC
  GND: Raspberry_Pi_1.GND, Right_door_sensor.pin_2, Left_door_sensor.pin_2, SI7021_temperature_sensor.GND, 2-Channel_Relay.GND
  N5: Raspberry_Pi_1.GPIO15, Right_door_sensor.pin_1
  N6: Raspberry_Pi_1.GPIO14, Left_door_sensor.pin_1
  5V: Raspberry_Pi_1.5V, 2-Channel_Relay.VCC

notes:
  Right garage door
  Left garage door

custom parts:
  Humidity Temperature Sensor SI7021: SI7021 sensor breakout board.
  2-Channel 5v Relay Shield: 2 Channel 5v Relay Shield w. 2x SPD-06VDC-SD-C
